// Logisim project CMP.circ as structural Verilog: 1 circuit, main circuit main
// CMP
module main (
  input  LT,
  input  EQ,
  input  GT,
  input  [2:0] CQ_QUERY,
  input  CR_WRITE,
  input  CLOCK,
  output [2:0] CR_VAL,
  output CQ_PASSED
);

  wire controlled_buffer_1_out, CR_WRITE_t, not_1_out, or_1_out, or_2_out;

  assign controlled_buffer_1_out = CR_WRITE_t ? CLOCK : 1'bz;  // Controlled_Buffer controlled_buffer_1
  Multiplexer #(.select(2)) multiplexer_1 (.in0(LT), .in2(EQ), .in3(GT));  // open: in1, out, sel, en
  Register #(.width(3)) CQ_Register (.D(CQ_QUERY), .Q({LT, EQ, GT}), .clk(controlled_buffer_1_out));  // open: en, clr
  or or_1 (or_1_out, EQ, GT);
  not not_1 (not_1_out, EQ);
  or or_2 (or_2_out, EQ, LT);
  Multiplexer #(.select(3), .enable("false")) multiplexer_2 (
    .in0(1'b0), .in1(GT), .in2(EQ), .in3(or_1_out), .in4(LT), .in5(not_1_out), .in6(or_2_out), .in7(1'b1),
    .out(CQ_PASSED), .sel(CQ_QUERY));

  assign CR_VAL = CQ_QUERY;

  // Other names for the same wires on the sheet: tunnel_t_t = GT; tunnel_t = EQ; tunnel = LT; clk = CLOCK;
  //   CQ[2:0] = CQ_QUERY

  // Notes on the sheet:
  //   CR MODULE
endmodule
