// Logisim project CPU.circ as structural Verilog: 1 circuit, main circuit main
// CPU
module main (
  input  [31:0] INSTRUCTION,
  input  [23:0] CURRENT_PC,
  input  CQ_PASSED,
  input  [31:0] REG_1_VAL,
  input  [31:0] REG_2_VAL,
  input  [31:0] REG_3_VAL,
  input  [31:0] ALU_RESULT,
  input  [31:0] MEM_OUT,
  output [23:0] JUMP_ADDRESS,
  output [2:0] CQ_QUERY,
  output CR_WRITE,
  output [3:0] REG_1_READ,
  output [3:0] REG_2_READ,
  output [3:0] REG_3_WRITE,
  output [31:0] REG_WRITE_VAL,
  output REG_WRITE,
  output [31:0] ALU_SOURCE_X,
  output [31:0] ALU_SOURCE_Y,
  output [3:0] ALU_OPERATION,
  output [23:0] MEM_ADDR,
  output [31:0] MEM_IN,
  output SHL,
  output SHR,
  output AND,
  output IOR,
  output XOR,
  output STU,
  output MUL,
  output DIV,
  output SUB,
  output ADD,
  output MLD,
  output MST,
  output STL,
  output LNK,
  output JMP,
  output MEM_WRITE
);

  wire ALUctr_0_out, ALUctr_1_out, ALUSrc_out, and_1_out, and_6_out, and_7_out, clk, comparator_1_eq,
       comparator_2_eq, comparator_3_eq, comparator_4_eq, comparator_5_eq, comparator_6_lt, CQ_Output,
       MemtoReg, not_2_out, not_3_out, not_4_out, not_5_out, nPC_sel, or_1_out, prev_jump, RegWrite_out;
  wire [0:0] ExtOp_out;
  wire [1:0] A_Type;
  wire [31:0] bit_extender_1_out, bit_extender_2_out, bit_extender_3_out, RI_OUT;

  Multiplexer #(.width(32), .enable("false")) multiplexer_1 (
    .in0(REG_2_VAL), .in1(RI_OUT), .out(ALU_SOURCE_Y), .sel(INSTRUCTION[24]));
  Multiplexer #(.width(4), .enable("false")) multiplexer_2 (
    .in0(INSTRUCTION[3:0]), .in1(INSTRUCTION[19:16]), .out(REG_2_READ), .sel(ALUSrc_out));
  assign bit_extender_1_out = {{16{1'b0}}, INSTRUCTION[15:0]};  // Bit_Extender bit_extender_1
  assign bit_extender_2_out = {{12{1'b0}}, INSTRUCTION[19:0]};  // Bit_Extender bit_extender_2
  assign bit_extender_3_out = {{8{1'b0}}, INSTRUCTION[23:0]};  // Bit_Extender bit_extender_3
  Multiplexer #(.width(32), .enable("false")) multiplexer_3 (
    .in0(MEM_OUT), .out(REG_WRITE_VAL), .sel(MemtoReg));  // open: in1
  Multiplexer #(.width(4), .enable("false")) multiplexer_4 (
    .in0(INSTRUCTION[19:16]), .in1(INSTRUCTION[3:0]), .out(REG_1_READ), .sel(and_1_out));
  and and_1 (and_1_out, ALUSrc_out, ~INSTRUCTION[24]);  // AND_Gate
  Multiplexer #(.width(32), .enable("false")) multiplexer_5 (
    .in0(MEM_IN), .out(ALU_RESULT), .sel(MEM_WRITE));  // open: in1
  Demultiplexer #(.select(2), .width(32)) demultiplexer_1 (
    .out0(REG_WRITE_VAL), .in(ALU_RESULT), .sel({CR_WRITE, MST}));  // open: out1, out2, out3, en
  Multiplexer #(.select(2), .width(32), .enable("false")) multiplexer_6 (
    .in0(bit_extender_1_out), .in1(bit_extender_2_out), .in2(bit_extender_3_out), .out(RI_OUT),
    .sel({JMP, ExtOp_out[0]}));  // open: in3
  Multiplexer #(.width(24), .enable("false")) multiplexer_7 (
    .in1(INSTRUCTION[23:0]), .out(JUMP_ADDRESS), .sel(JMP));  // open: in0
  Comparator #(.width(4), .mode("unsigned")) comparator_1 (
    .a(INSTRUCTION[31:28]), .b(4'b1111), .eq(comparator_1_eq));  // open: gt, lt
  Comparator #(.width(4), .mode("unsigned")) comparator_2 (
    .a(INSTRUCTION[31:28]), .b(4'b1010), .eq(comparator_2_eq));  // open: gt, lt
  Comparator #(.width(4), .mode("unsigned")) comparator_3 (
    .a(INSTRUCTION[31:28]), .b(4'b1011), .eq(comparator_3_eq));  // open: gt, lt
  or ALUSrc (ALUSrc_out, STU, SUB, STL, LNK);
  not not_1 (REG_WRITE, RegWrite_out);
  or RegWrite (RegWrite_out, MST, CR_WRITE, JMP);
  // OR_Gate ALUctr_0 has open pins: out=ALUctr_0_out
  // OR_Gate ALUctr_1 has open pins: out=ALUctr_1_out
  // AND_Gate and_2 has open pins: in0=comparator_1_eq, in1=prev_jump, in2=CQ_Output, out=open
  // AND_Gate and_3 has open pins: in0=comparator_2_eq, in1=prev_jump, in2=CQ_Output, out=open
  // AND_Gate and_4 has open pins: in0=comparator_3_eq, in1=prev_jump, in2=CQ_Output, out=open
  not not_2 (not_2_out, INSTRUCTION[28]);
  not not_3 (not_3_out, INSTRUCTION[29]);
  not not_4 (not_4_out, INSTRUCTION[30]);
  not not_5 (not_5_out, INSTRUCTION[31]);
  buf MemWrite (MEM_WRITE, MST);  // OR_Gate
  buf u_MemtoReg (MemtoReg, MLD);  // OR_Gate
  buf u_nPC_sel (nPC_sel, JMP);  // OR_Gate
  or ExtOp (ExtOp_out[0], STL, CR_WRITE, LNK);
  and u_SHL (SHL, not_2_out, not_3_out, not_4_out, not_5_out);
  and u_SHR (SHR, INSTRUCTION[28], not_3_out, not_4_out, not_5_out);
  and AND_5 (AND, not_2_out, INSTRUCTION[28], not_4_out, not_5_out);
  and u_IOR (IOR, INSTRUCTION[28], INSTRUCTION[29], not_4_out, not_5_out);
  Comparator #(.width(4), .mode("unsigned")) comparator_4 (
    .a(INSTRUCTION[31:28]), .b(4'b1110), .eq(comparator_4_eq));  // open: gt, lt
  and u_XOR (XOR, not_2_out, not_3_out, INSTRUCTION[30], not_5_out);
  Comparator #(.width(2)) comparator_5 (.a(2'b01), .b(A_Type), .eq(comparator_5_eq));  // open: gt, lt
  Comparator #(.width(4), .mode("unsigned")) comparator_6 (
    .a(INSTRUCTION[31:28]), .b(4'b1011), .lt(comparator_6_lt));  // open: gt, eq
  and u_STU (STU, INSTRUCTION[28], not_4_out, INSTRUCTION[30], not_5_out);
  and and_6 (and_6_out, comparator_5_eq, prev_jump, CQ_Output);
  or or_1 (or_1_out, comparator_6_lt, comparator_4_eq);
  and u_MUL (MUL, not_2_out, INSTRUCTION[29], INSTRUCTION[30], not_5_out);
  and and_7 (and_7_out, CQ_Output, prev_jump, clk, or_1_out);
  and u_DIV (DIV, INSTRUCTION[28], INSTRUCTION[29], INSTRUCTION[30], not_5_out);
  and u_SUB (SUB, not_2_out, not_3_out, not_4_out, INSTRUCTION[31]);
  and u_MLD (MLD, not_2_out, INSTRUCTION[29], not_4_out, INSTRUCTION[31]);
  and u_ADD (ADD, INSTRUCTION[28], not_3_out, not_4_out, INSTRUCTION[31]);
  and u_MST (MST, INSTRUCTION[28], not_3_out, not_4_out, INSTRUCTION[31]);
  and u_STL (STL, not_2_out, not_4_out, INSTRUCTION[30], INSTRUCTION[31]);
  and CMP (CR_WRITE, INSTRUCTION[28], not_3_out, INSTRUCTION[30], INSTRUCTION[31]);
  and u_LNK (LNK, not_2_out, INSTRUCTION[29], INSTRUCTION[30], INSTRUCTION[31]);
  and u_JMP (JMP, INSTRUCTION[28], INSTRUCTION[29], INSTRUCTION[30], INSTRUCTION[31]);

  assign ALU_OPERATION = INSTRUCTION[31:28];
  assign ALU_SOURCE_X = REG_1_VAL;
  assign CQ_QUERY = INSTRUCTION[27:25];
  assign REG_3_WRITE = INSTRUCTION[23:20];

  // Other names for the same wires on the sheet: CMP = CR_WRITE; RI[3:0] = INSTRUCTION[3:0];
  //   IMM[11:0] = INSTRUCTION[15:4]; RS[3:0] = INSTRUCTION[19:16]; RD[3:0] = INSTRUCTION[23:20];
  //   IS_RI = INSTRUCTION[24]; _CQ[2:0] = INSTRUCTION[27:25]; OP_Code[3:0] = INSTRUCTION[31:28]; memStore = MEM_WRITE

  // Notes on the sheet:
  //   INSTRUCTION MODULE
  //   CR MODULE
  //   REGISTER FILE MODULE
  //   ALU MODULE
  //   MEMORY MODULE
  //   Control
  //   Can REG write?
  //   Is this  set CQ command?
endmodule
