// Logisim project PIP.circ as structural Verilog: 1 circuit, main circuit main
// PIP
module main (
  input  CQ_PASSED,
  input  [31:0] INSTRUCTION_IN,
  input  [23:0] PC_IN,
  input  CLOCK,
  output [31:0] INSTRUCTION_OUT,
  output [23:0] PC_OUT
);

  Multiplexer #(.width(32)) multiplexer_1 (
    .in0({32{1'b0}}), .in1(INSTRUCTION_IN), .out(INSTRUCTION_OUT), .sel(CQ_PASSED));  // open: en
  Register #(.width(24)) register_1 (.D(PC_IN), .en(CQ_PASSED), .Q(PC_OUT), .clk(CLOCK));  // open: clr

  // Other names for the same wires on the sheet: clk = CLOCK; cqpass = CQ_PASSED

  // Notes on the sheet:
  //   PIPELINE MODULE
endmodule
